# Fritzing sketch Yukari (saved by Fritzing 0.9.2b)
breadboards: 2

parts:
  Part1 = FTDI Basic Programmer
  SW1 = DIP Switch 8 Position [package=dipswitch-08]
  ADuM1 = ADuM3221 [package="DIP (Dual Inline) [THT]"]
  U1 = mystery part, 3 pins [chip_label=STR]
  U3 = mystery part, 3 pins [chip_label=THR]
  U2 = mystery part, 2 pins [chip_label=CAM]
  U4 = mystery part, 8 pins [chip_label=GP-2106]
  IC1 = Loginator [chip_label=Loginator package="DIP (Dual Inline) [THT]"]

nets:
  N1: Part1.RXI, IC1.TX0
  N2: Part1.TXO, SW1.15
  N3: Part1.POWER, IC1.VBUS
  GND: Part1.GND, SW1.14, ADuM1.GNDI, U4.pin6, IC1.GND3
  N4: SW1.1, SW1.2, IC1.RX0
  N5: SW1.3, IC1.BSL/SDA1
  N6: SW1.16, U4.pin3
  N7: ADuM1.VCCI, IC1.VCC2
  N8: ADuM1.INA, IC1.TX1
  N9: ADuM1.INB, IC1.RX1
  N10: ADuM1.GNDO, U1.pin3, U3.pin1, U2.pin1
  N11: ADuM1.OUTB, U3.pin3
  N12: ADuM1.OUTA, U1.pin1
  N13: ADuM1.VCCO, U1.pin2, U3.pin2, U2.pin2
  N14: U4.pin1, IC1.AD5
  N15: U4.pin5, IC1.VBAT
  GND1: IC1.GND1, IC1.GND2, IC1.SDA0
  N16: IC1.VCC1, IC1.SCL0

custom parts:
  ADuM3221: Analog Devices ADuM3221 magnetic isolator. This provides two channels of digital connectivity from one voltage domain to another, with no direct electrical connectivity between the domains. The actual part is an SOT-8 soldered to a breakout board.
  Loginator: Kwan Systems Loginator v1.1 -
